// Digital circuit cpu.dig as structural Verilog
module cpu (
  input  clk,
  input  clk_2,
  input  RESET
);

  wire _4x8bit_mux_1_p6, condition_checker_1_skip, nand_1_out, nand_4_out, nand_5_out, nand_6_out,
       oprom_1_bssel, oprom_1_fwen, oprom_1_massel, oprom_1_mwen, oprom_1_rwen, program_memory_1_p5,
       program_memory_1_p6, program_memory_1_p7;
  wire [1:0] nand_2_out, oprom_1_pcssel, oprom_1_rssel;
  wire [2:0] program_memory_1_p3, program_memory_1_p4;
  wire [3:0] program_memory_1_p2;
  wire [4:0] _8bit_alu_1_flags;
  wire [7:0] _2x8bit_mux_1_out, _4x8bit_mux_1_p3, _4x8bit_mux_1_p4, program_memory_1_p8, register_file_1_p9;
  wire [7:5] _8bit_alu_1_flags_2;
  wire [15:0] _2x16bit_mux_1_p4, _4x8bit_mux_1_p5, _4x16bit_mux_1_out, _16bit_incrementer_1_out,
       program_memory_1_p1, program_memory_1_p9;

  nand nand_1 (nand_1_out, clk_2, clk_2);
  // program_memory program_memory_1: pin names not known; wires that end beside it: program_memory_1_p1, program_memory_1_p2, program_memory_1_p3, program_memory_1_p4, program_memory_1_p5, program_memory_1_p6, program_memory_1_p7, program_memory_1_p8, program_memory_1_p9
  program_counter program_counter_1 (.CLK(clk_2), .W(_4x16bit_mux_1_out), .R(program_memory_1_p1));
  _4x16bit_mux _4x16bit_mux_1 (
    .SEL(nand_2_out), .IN0({16{1'b0}}), .IN1(_16bit_incrementer_1_out), .IN2(_4x8bit_mux_1_p5),
    .IN3(program_memory_1_p9), .OUT(_4x16bit_mux_1_out));
  condition_checker condition_checker_1 (
    .FLAGS(_8bit_alu_1_flags), .COND(program_memory_1_p3), .SKIP(condition_checker_1_skip));
  oprom oprom_1 (
    .OPCODE(program_memory_1_p2), .SKIP(condition_checker_1_skip), .RWEN(oprom_1_rwen), .FWEN(oprom_1_fwen),
    .MWEN(oprom_1_mwen), .BSSEL(oprom_1_bssel), .MASSEL(oprom_1_massel), .RSSEL(oprom_1_rssel),
    .PCSSEL(oprom_1_pcssel));
  _16bit_incrementer _16bit_incrementer_1 (.IN(program_memory_1_p1), .OUT(_16bit_incrementer_1_out));
  // _4x8bit_mux _4x8bit_mux_1: pin names not known; wires that end beside it: oprom_1_rssel, program_memory_1_p8, _4x8bit_mux_1_p3, _4x8bit_mux_1_p4, _4x8bit_mux_1_p5[7:0], _4x8bit_mux_1_p6
  nand nand_2 (nand_2_out[1], nand_4_out, nand_4_out);
  nand nand_3 (nand_2_out[0], nand_5_out, nand_5_out);
  nand nand_4 (nand_4_out, RESET, oprom_1_pcssel[1]);
  nand nand_5 (nand_5_out, RESET, oprom_1_pcssel[0]);
  // register_file register_file_1: pin names not known; wires that end beside it: nand_1_out, oprom_1_rwen, _4x8bit_mux_1_p6, program_memory_1_p6, program_memory_1_p5, program_memory_1_p7, _4x8bit_mux_1_p5[7:0], _4x8bit_mux_1_p5[15:8], register_file_1_p9
  // _2x16bit_mux _2x16bit_mux_1: pin names not known; wires that end beside it: oprom_1_massel, {register_file_1_p9, _4x8bit_mux_1_p5[7:0]}, program_memory_1_p9, _2x16bit_mux_1_p4
  _2x8bit_mux _2x8bit_mux_1 (
    .SEL(oprom_1_bssel), .B(_4x8bit_mux_1_p5[15:8]), .A(program_memory_1_p8), .OUT(_2x8bit_mux_1_out));
  nand nand_6 (nand_6_out, oprom_1_mwen, oprom_1_mwen);
  _8bit_alu _8bit_alu_1 (
    .A(_4x8bit_mux_1_p5[7:0]), .B(_2x8bit_mux_1_out), .OP(program_memory_1_p4), .CLK(nand_1_out),
    .WFLAGEN(oprom_1_fwen), .FLAGS({_8bit_alu_1_flags_2, _8bit_alu_1_flags}), .RESULT(_4x8bit_mux_1_p4));
  RAMDualPort #(.AddrBits(16), .Bits(8)) ramdualport_1 (
    .A(_2x16bit_mux_1_p4), .Din(_4x8bit_mux_1_p5[15:8]), .str(oprom_1_mwen), .C(clk), .ld(nand_6_out),
    .D(_4x8bit_mux_1_p3));

  // Notes on the sheet:
  //   clk: Hz: 100
endmodule
